// Logisim project ALU.circ as structural Verilog: 11 circuits, main circuit ALU
module ALU (
  input  [15:0] A,
  input  [2:0] S,
  input  [15:0] B,
  output [15:0] out_4,
  output Overflow
);

  wire div_1_div_0, mult_1_overflow, sub_1_overflow, sum_1_overflow;
  wire [15:0] div_1_quociente, div_1_resto, mult_1_resultado, sub_1_resultado, sum_1_resultado;

  Sum sum_1 (.A(A), .B(B), .Resultado(sum_1_resultado), .Overflow(sum_1_overflow));
  Sub sub_1 (.Minuendo(A), .Subtraendo(B), .Resultado(sub_1_resultado), .Overflow(sub_1_overflow));
  Mult mult_1 (.X(A), .Y(B), .Resultado(mult_1_resultado), .Overflow(mult_1_overflow));
  Div div_1 (.Dividendo(A), .Divisor(B), .Quociente(div_1_quociente), .Resto(div_1_resto), .Div_0(div_1_div_0));
  Multiplexer #(.select(3), .width(16), .enable("false")) multiplexer_1 (
    .in0(sum_1_resultado), .in1(sub_1_resultado), .in2(mult_1_resultado), .in3(div_1_quociente),
    .in4(div_1_resto), .out(out_4), .sel(S));  // open: in5, in6, in7
  // Seletor1 seletor1_1: pin names not known; wires that end beside it: sum_1_overflow, sub_1_overflow, mult_1_overflow, div_1_div_0, S, Overflow
endmodule

module Seletor1 (
  input  [2:0] \Operação ,
  input  \Adição ,
  input  \Subtração ,
  input  \Multiplicação ,
  input  \Divisão ,
  output Resultado
);

  wire and_1_out, and_2_out, and_3_out, and_4_out, not_1_out, not_2_out, not_3_out, or_1_out;

  not not_1 (not_1_out, \Operação [2]);
  not not_2 (not_2_out, \Operação [1]);
  not not_3 (not_3_out, \Operação [0]);
  and and_1 (and_1_out, \Divisão , not_1_out, \Operação [1], \Operação [0]);
  and and_2 (and_2_out, \Adição , not_1_out, not_2_out, not_3_out);
  and and_3 (and_3_out, \Subtração , not_1_out, not_2_out, \Operação [0]);
  and and_4 (and_4_out, \Multiplicação , not_1_out, \Operação [1], not_3_out);
  or or_1 (or_1_out, and_1_out, \Operação [2]);
  or or_2 (Resultado, and_2_out, and_3_out, and_4_out, or_1_out);
endmodule

module Seletor8 (
  input  [2:0] \Operação ,
  input  [7:0] \Adição ,
  input  [7:0] \Subtração ,
  input  [7:0] \Multiplicação ,
  input  [7:0] \Divisão ,
  input  [7:0] Resto,
  output [7:0] Resultado
);

  wire and_1_out, and_2_out, and_3_out, and_4_out, and_5_out, and_6_out, and_7_out, and_8_out, and_9_out,
       and_10_out, and_11_out, and_12_out, and_13_out, and_14_out, and_15_out, and_16_out, and_17_out,
       and_18_out, and_19_out, and_20_out, and_21_out, and_22_out, and_23_out, and_24_out, and_25_out,
       and_26_out, and_27_out, and_28_out, and_29_out, and_30_out, and_31_out, and_32_out, and_33_out,
       and_34_out, and_35_out, and_36_out, and_37_out, and_38_out, and_39_out, and_40_out, not_1_out,
       not_2_out, not_3_out;

  not not_1 (not_1_out, \Operação [2]);
  not not_2 (not_2_out, \Operação [1]);
  not not_3 (not_3_out, \Operação [0]);
  and and_1 (and_1_out, \Adição [0], not_1_out, not_2_out, not_3_out);
  and and_2 (and_2_out, \Adição [1], not_1_out, not_2_out, not_3_out);
  and and_3 (and_3_out, \Adição [2], not_1_out, not_2_out, not_3_out);
  and and_4 (and_4_out, \Adição [3], not_1_out, not_2_out, not_3_out);
  and and_5 (and_5_out, \Adição [4], not_1_out, not_2_out, not_3_out);
  and and_6 (and_6_out, \Adição [5], not_1_out, not_2_out, not_3_out);
  and and_7 (and_7_out, \Adição [6], not_1_out, not_2_out, not_3_out);
  and and_8 (and_8_out, \Adição [7], not_1_out, not_2_out, not_3_out);
  and and_9 (and_9_out, \Subtração [0], not_1_out, not_2_out, \Operação [0]);
  and and_10 (and_10_out, \Subtração [1], not_1_out, not_2_out, \Operação [0]);
  and and_11 (and_11_out, \Subtração [2], not_1_out, not_2_out, \Operação [0]);
  and and_12 (and_12_out, \Subtração [3], not_1_out, not_2_out, \Operação [0]);
  and and_13 (and_13_out, \Subtração [4], not_1_out, not_2_out, \Operação [0]);
  and and_14 (and_14_out, \Subtração [5], not_1_out, not_2_out, \Operação [0]);
  and and_15 (and_15_out, \Subtração [6], not_1_out, not_2_out, \Operação [0]);
  and and_16 (and_16_out, \Subtração [7], not_1_out, not_2_out, \Operação [0]);
  and and_17 (and_17_out, \Multiplicação [0], not_1_out, \Operação [1], not_3_out);
  and and_18 (and_18_out, \Multiplicação [1], not_1_out, not_3_out);
  and and_19 (and_19_out, \Multiplicação [2], not_1_out, \Operação [1], not_3_out);
  and and_20 (and_20_out, \Multiplicação [3], not_1_out, \Operação [1], not_3_out);
  and and_21 (and_21_out, \Multiplicação [4], not_1_out, not_3_out);
  and and_22 (and_22_out, \Multiplicação [5], not_1_out, \Operação [1], not_3_out);
  and and_23 (and_23_out, \Multiplicação [6], not_1_out, \Operação [1], not_3_out);
  and and_24 (and_24_out, \Multiplicação [7], not_1_out, \Operação [1], not_3_out);
  and and_25 (and_25_out, \Divisão [0], not_1_out, \Operação [1], \Operação [0]);
  and and_26 (and_26_out, \Divisão [1], not_1_out, \Operação [1], \Operação [0]);
  and and_27 (and_27_out, \Divisão [2], not_1_out, \Operação [1], \Operação [0]);
  and and_28 (and_28_out, \Divisão [3], not_1_out, \Operação [1], \Operação [0]);
  and and_29 (and_29_out, \Divisão [4], not_1_out, \Operação [1], \Operação [0]);
  and and_30 (and_30_out, \Divisão [5], not_1_out, \Operação [1], \Operação [0]);
  and and_31 (and_31_out, \Divisão [6], not_1_out, \Operação [1], \Operação [0]);
  and and_32 (and_32_out, \Divisão [7], not_1_out, \Operação [1], \Operação [0]);
  and and_33 (and_33_out, Resto[0], \Operação [2]);
  and and_34 (and_34_out, Resto[1], \Operação [2]);
  and and_35 (and_35_out, Resto[2], \Operação [2]);
  and and_36 (and_36_out, Resto[3], \Operação [2]);
  and and_37 (and_37_out, Resto[4], \Operação [2]);
  and and_38 (and_38_out, Resto[5], \Operação [2]);
  and and_39 (and_39_out, Resto[6], \Operação [2]);
  and and_40 (and_40_out, Resto[7], \Operação [2]);
  or or_1 (Resultado[0], and_1_out, and_9_out, and_17_out, and_25_out, and_33_out);
  or or_2 (Resultado[1], and_2_out, and_10_out, and_18_out, and_26_out, and_34_out);
  or or_3 (Resultado[2], and_3_out, and_11_out, and_19_out, and_27_out, and_35_out);
  or or_4 (Resultado[3], and_4_out, and_12_out, and_20_out, and_28_out, and_36_out);
  or or_5 (Resultado[4], and_5_out, and_13_out, and_21_out, and_29_out, and_37_out);
  or or_6 (Resultado[5], and_6_out, and_14_out, and_22_out, and_30_out, and_38_out);
  or or_7 (Resultado[6], and_7_out, and_15_out, and_23_out, and_31_out, and_39_out);
  or or_8 (Resultado[7], and_8_out, and_16_out, and_24_out, and_32_out, and_40_out);
endmodule

module Sum (
  input  [15:0] A,
  input  [15:0] B,
  output [15:0] Resultado,
  output Overflow
);

  wire full_adder_1_cout, full_adder_2_cout, full_adder_3_cout, full_adder_4_cout, full_adder_5_cout,
       full_adder_6_cout, full_adder_7_cout, full_adder_8_cout, full_adder_9_cout, full_adder_10_cout,
       full_adder_11_cout, full_adder_12_cout, full_adder_13_cout, full_adder_14_cout, half_adder_1_carry;

  Half_Adder half_adder_1 (.A(A[0]), .B(B[0]), .Resultado(Resultado[0]), .Carry(half_adder_1_carry));
  Full_Adder full_adder_1 (.A(A[1]), .B(B[1]), .r(Resultado[1]), .cout(full_adder_1_cout), .cin(half_adder_1_carry));
  Full_Adder full_adder_2 (.A(A[2]), .B(B[2]), .r(Resultado[2]), .cout(full_adder_2_cout), .cin(full_adder_1_cout));
  Full_Adder full_adder_3 (.A(A[3]), .B(B[3]), .r(Resultado[3]), .cout(full_adder_3_cout), .cin(full_adder_2_cout));
  Full_Adder full_adder_4 (.A(A[4]), .B(B[4]), .r(Resultado[4]), .cout(full_adder_4_cout), .cin(full_adder_3_cout));
  Full_Adder full_adder_5 (.A(A[5]), .B(B[5]), .r(Resultado[5]), .cout(full_adder_5_cout), .cin(full_adder_4_cout));
  Full_Adder full_adder_6 (.A(A[6]), .B(B[6]), .r(Resultado[6]), .cout(full_adder_6_cout), .cin(full_adder_5_cout));
  Full_Adder full_adder_7 (.A(A[7]), .B(B[7]), .r(Resultado[7]), .cout(full_adder_7_cout), .cin(full_adder_6_cout));
  Full_Adder full_adder_8 (.A(A[8]), .B(B[8]), .r(Resultado[8]), .cout(full_adder_8_cout), .cin(full_adder_7_cout));
  Full_Adder full_adder_9 (.A(A[9]), .B(B[9]), .r(Resultado[9]), .cout(full_adder_9_cout), .cin(full_adder_8_cout));
  Full_Adder full_adder_10 (
    .A(A[10]), .B(B[10]), .r(Resultado[10]), .cout(full_adder_10_cout), .cin(full_adder_9_cout));
  Full_Adder full_adder_11 (
    .A(A[11]), .B(B[11]), .r(Resultado[11]), .cout(full_adder_11_cout), .cin(full_adder_10_cout));
  Full_Adder full_adder_12 (
    .A(A[12]), .B(B[12]), .r(Resultado[12]), .cout(full_adder_12_cout), .cin(full_adder_11_cout));
  Full_Adder full_adder_13 (
    .A(A[13]), .B(B[13]), .r(Resultado[13]), .cout(full_adder_13_cout), .cin(full_adder_12_cout));
  Full_Adder full_adder_14 (
    .A(A[14]), .B(B[14]), .r(Resultado[14]), .cout(full_adder_14_cout), .cin(full_adder_13_cout));
  Full_Adder full_adder_15 (.A(A[15]), .B(B[15]), .r(Resultado[15]), .cout(Overflow), .cin(full_adder_14_cout));
endmodule

module Full_Adder (
  input  cin,
  input  A,
  input  B,
  output r,
  output cout
);

  wire and_1_out, and_2_out, xor_1_out;

  and and_1 (and_1_out, A, B);
  xor xor_1 (xor_1_out, A, B);
  or or_1 (cout, and_1_out, and_2_out);
  and and_2 (and_2_out, cin, xor_1_out);
  xor xor_2 (r, cin, xor_1_out);
endmodule

module Half_Adder (
  input  A,
  input  B,
  output Resultado,
  output Carry
);

  xor xor_1 (Resultado, A, B);
  and and_1 (Carry, A, B);
endmodule

module Comp2 (
  input  [15:0] Entrada,
  output [15:0] Resultado
);

  wire [15:0] not_1_out;

  assign not_1_out = ~Entrada;  // NOT_Gate not_1, 16 bits wide
  Sum sum_1 (.A(16'h1), .B(not_1_out), .Resultado(Resultado));  // open: Overflow
endmodule

module Sub (
  input  [15:0] Minuendo,
  input  [15:0] Subtraendo,
  output [15:0] Resultado,
  output Overflow
);

  wire [15:0] comp2_1_resultado;

  Comp2 comp2_1 (.Entrada(Subtraendo), .Resultado(comp2_1_resultado));
  Sum sum_1 (.A(Minuendo), .B(comp2_1_resultado), .Resultado(Resultado), .Overflow(Overflow));
endmodule

module Mult (
  input  [15:0] X,
  input  [15:0] Y,
  output [15:0] Resultado,
  output Overflow
);

  wire and_1_out, and_2_out, and_3_out, and_4_out, and_5_out, and_6_out, and_7_out, and_8_out, and_9_out,
       and_10_out, and_11_out, and_12_out, and_13_out, and_14_out, and_15_out, and_16_out, and_17_out,
       and_18_out, and_19_out, and_20_out, and_21_out, and_22_out, and_23_out, and_24_out, and_25_out,
       and_26_out, and_27_out, and_28_out, and_29_out, and_30_out, and_31_out, and_32_out, and_33_out,
       and_34_out, and_35_out, and_36_out, and_37_out, and_38_out, and_39_out, and_40_out, and_41_out,
       and_42_out, and_43_out, and_45_out, and_46_out, and_47_out, and_48_out, and_49_out, and_50_out,
       full_adder_1_cout, full_adder_1_r, full_adder_2_cout, full_adder_2_r, full_adder_3_cout,
       full_adder_3_r, full_adder_4_cout, full_adder_4_r, full_adder_5_cout, full_adder_5_r,
       full_adder_6_cout, full_adder_6_r, full_adder_7_cout, full_adder_7_r, full_adder_8_cout,
       full_adder_8_r, full_adder_9_cout, full_adder_9_r, full_adder_10_cout, full_adder_10_r,
       full_adder_11_cout, full_adder_11_r, full_adder_12_cout, full_adder_12_r, full_adder_13_cout,
       full_adder_13_r, full_adder_14_cout, full_adder_14_r, full_adder_15_cout, full_adder_15_r,
       full_adder_16_cout, full_adder_16_r, full_adder_17_cout, full_adder_17_r, full_adder_18_cout,
       full_adder_18_r, full_adder_19_cout, full_adder_19_r, full_adder_20_cout, full_adder_20_r,
       full_adder_21_cout, full_adder_21_r, full_adder_22_cout, full_adder_22_r, full_adder_23_cout,
       full_adder_23_r, full_adder_24_cout, full_adder_24_r, full_adder_25_cout, full_adder_25_r,
       full_adder_26_cout, full_adder_26_r, full_adder_27_cout, full_adder_27_r, full_adder_28_cout,
       full_adder_28_r, full_adder_29_cout, full_adder_29_r, full_adder_30_cout, full_adder_30_r,
       full_adder_31_cout, full_adder_31_r, full_adder_32_cout, full_adder_32_r, full_adder_33_cout,
       full_adder_33_r, full_adder_34_cout, full_adder_34_r, full_adder_35_cout, full_adder_35_r,
       full_adder_36_cout, full_adder_36_r, full_adder_37_cout, full_adder_37_r, full_adder_38_cout,
       full_adder_38_r, full_adder_39_cout, full_adder_39_r, full_adder_40_cout, full_adder_40_r,
       full_adder_41_cout, full_adder_41_r, full_adder_42_cout, full_adder_42_r, full_adder_43_cout,
       full_adder_43_r, full_adder_44_cout, full_adder_44_r, full_adder_45_cout, full_adder_45_r,
       full_adder_46_cout, full_adder_46_r, full_adder_47_cout, full_adder_47_r, full_adder_48_cout,
       full_adder_48_r, full_adder_49_cout, full_adder_49_r, half_adder_1_resultado, half_adder_2_carry,
       half_adder_3_carry, half_adder_4_carry, half_adder_5_carry, half_adder_6_carry, half_adder_7_carry,
       half_adder_8_carry, nand_1_out, nand_2_out, nand_3_out, nand_4_out, nand_5_out, nand_6_out,
       nand_7_out, nand_8_out, nand_9_out, nand_10_out, nand_11_out, nand_12_out, nand_13_out, nand_14_out;

  Half_Adder half_adder_1 (.A(1'b1), .B(full_adder_7_cout), .Resultado(half_adder_1_resultado));  // open: Carry
  nand nand_1 (nand_1_out, X[15], Y[8]);
  nand nand_2 (nand_2_out, X[15], Y[9]);
  Full_Adder full_adder_1 (
    .A(nand_2_out), .B(1'b1), .r(full_adder_1_r), .cout(full_adder_1_cout), .cin(full_adder_14_cout));
  nand nand_3 (nand_3_out, X[15], Y[10]);
  Full_Adder full_adder_2 (
    .A(nand_3_out), .B(full_adder_1_cout), .r(full_adder_2_r), .cout(full_adder_2_cout),
    .cin(full_adder_8_cout));
  nand nand_4 (nand_4_out, X[15], Y[11]);
  Full_Adder full_adder_3 (
    .A(nand_4_out), .B(full_adder_2_cout), .r(full_adder_3_r), .cout(full_adder_3_cout),
    .cin(full_adder_9_cout));
  nand nand_5 (nand_5_out, X[15], Y[12]);
  Full_Adder full_adder_4 (
    .A(nand_5_out), .B(full_adder_3_cout), .r(full_adder_4_r), .cout(full_adder_4_cout),
    .cin(full_adder_10_cout));
  nand nand_6 (nand_6_out, X[15], Y[13]);
  Full_Adder full_adder_5 (
    .A(nand_6_out), .B(full_adder_4_cout), .r(full_adder_5_r), .cout(full_adder_5_cout),
    .cin(full_adder_11_cout));
  nand nand_7 (nand_7_out, X[15], Y[14]);
  Full_Adder full_adder_6 (
    .A(nand_7_out), .B(full_adder_5_cout), .r(full_adder_6_r), .cout(full_adder_6_cout),
    .cin(full_adder_12_cout));
  and and_1 (and_1_out, X[15], Y[15]);
  Full_Adder full_adder_7 (
    .A(and_1_out), .B(full_adder_6_cout), .r(full_adder_7_r), .cout(full_adder_7_cout),
    .cin(full_adder_13_cout));
  and and_2 (and_2_out, X[14], Y[10]);
  Full_Adder full_adder_8 (
    .A(and_2_out), .B(full_adder_1_r), .r(full_adder_8_r), .cout(full_adder_8_cout), .cin(full_adder_15_cout));
  and and_3 (and_3_out, X[14], Y[11]);
  Full_Adder full_adder_9 (
    .A(and_3_out), .B(full_adder_2_r), .r(full_adder_9_r), .cout(full_adder_9_cout), .cin(full_adder_16_cout));
  and and_4 (and_4_out, X[14], Y[12]);
  Full_Adder full_adder_10 (
    .A(and_4_out), .B(full_adder_3_r), .r(full_adder_10_r), .cout(full_adder_10_cout),
    .cin(full_adder_18_cout));
  and and_5 (and_5_out, X[14], Y[13]);
  Full_Adder full_adder_11 (
    .A(and_5_out), .B(full_adder_4_r), .r(full_adder_11_r), .cout(full_adder_11_cout),
    .cin(full_adder_19_cout));
  and and_6 (and_6_out, X[14], Y[14]);
  Full_Adder full_adder_12 (
    .A(and_6_out), .B(full_adder_5_r), .r(full_adder_12_r), .cout(full_adder_12_cout),
    .cin(full_adder_20_cout));
  nand nand_8 (nand_8_out, X[14], Y[15]);
  Full_Adder full_adder_13 (
    .A(nand_8_out), .B(full_adder_6_r), .r(full_adder_13_r), .cout(full_adder_13_cout),
    .cin(full_adder_21_cout));
  and and_7 (and_7_out, X[14], Y[8]);
  and and_8 (and_8_out, X[14], Y[9]);
  Full_Adder full_adder_14 (
    .A(and_8_out), .B(nand_1_out), .r(full_adder_14_r), .cout(full_adder_14_cout), .cin(full_adder_17_cout));
  and and_9 (and_9_out, X[13], Y[10]);
  Full_Adder full_adder_15 (
    .A(and_9_out), .B(full_adder_14_r), .r(full_adder_15_r), .cout(full_adder_15_cout),
    .cin(full_adder_23_cout));
  and and_10 (and_10_out, X[13], Y[11]);
  Full_Adder full_adder_16 (
    .A(and_10_out), .B(full_adder_8_r), .r(full_adder_16_r), .cout(full_adder_16_cout),
    .cin(full_adder_24_cout));
  and and_11 (and_11_out, X[13], Y[8]);
  and and_12 (and_12_out, X[13], Y[9]);
  Full_Adder full_adder_17 (
    .A(and_12_out), .B(and_7_out), .r(full_adder_17_r), .cout(full_adder_17_cout), .cin(full_adder_22_cout));
  and and_13 (and_13_out, X[13], Y[12]);
  Full_Adder full_adder_18 (
    .A(and_13_out), .B(full_adder_9_r), .r(full_adder_18_r), .cout(full_adder_18_cout),
    .cin(full_adder_25_cout));
  and and_14 (and_14_out, X[13], Y[13]);
  Full_Adder full_adder_19 (
    .A(and_14_out), .B(full_adder_10_r), .r(full_adder_19_r), .cout(full_adder_19_cout),
    .cin(full_adder_26_cout));
  and and_15 (and_15_out, X[13], Y[14]);
  Full_Adder full_adder_20 (
    .A(and_15_out), .B(full_adder_11_r), .r(full_adder_20_r), .cout(full_adder_20_cout),
    .cin(full_adder_27_cout));
  nand nand_9 (nand_9_out, X[13], Y[15]);
  Full_Adder full_adder_21 (
    .A(nand_9_out), .B(full_adder_12_r), .r(full_adder_21_r), .cout(full_adder_21_cout),
    .cin(full_adder_28_cout));
  and and_16 (and_16_out, X[12], Y[8]);
  and and_17 (and_17_out, X[12], Y[9]);
  Full_Adder full_adder_22 (
    .A(and_17_out), .B(and_11_out), .r(full_adder_22_r), .cout(full_adder_22_cout), .cin(full_adder_32_cout));
  and and_18 (and_18_out, X[12], Y[10]);
  Full_Adder full_adder_23 (
    .A(and_18_out), .B(full_adder_17_r), .r(full_adder_23_r), .cout(full_adder_23_cout),
    .cin(full_adder_29_cout));
  and and_19 (and_19_out, X[12], Y[11]);
  Full_Adder full_adder_24 (
    .A(and_19_out), .B(full_adder_15_r), .r(full_adder_24_r), .cout(full_adder_24_cout),
    .cin(full_adder_30_cout));
  and and_20 (and_20_out, X[12], Y[12]);
  Full_Adder full_adder_25 (
    .A(and_20_out), .B(full_adder_16_r), .r(full_adder_25_r), .cout(full_adder_25_cout),
    .cin(full_adder_31_cout));
  and and_21 (and_21_out, X[12], Y[13]);
  Full_Adder full_adder_26 (
    .A(and_21_out), .B(full_adder_18_r), .r(full_adder_26_r), .cout(full_adder_26_cout),
    .cin(full_adder_35_cout));
  and and_22 (and_22_out, X[12], Y[14]);
  Full_Adder full_adder_27 (
    .A(and_22_out), .B(full_adder_19_r), .r(full_adder_27_r), .cout(full_adder_27_cout),
    .cin(full_adder_36_cout));
  nand nand_10 (nand_10_out, X[12], Y[15]);
  Full_Adder full_adder_28 (
    .A(nand_10_out), .B(full_adder_20_r), .r(full_adder_28_r), .cout(full_adder_28_cout),
    .cin(full_adder_37_cout));
  and and_23 (and_23_out, X[11], Y[10]);
  Full_Adder full_adder_29 (
    .A(and_23_out), .B(full_adder_22_r), .r(full_adder_29_r), .cout(full_adder_29_cout),
    .cin(full_adder_33_cout));
  and and_24 (and_24_out, X[11], Y[11]);
  Full_Adder full_adder_30 (
    .A(and_24_out), .B(full_adder_23_r), .r(full_adder_30_r), .cout(full_adder_30_cout),
    .cin(full_adder_34_cout));
  and and_25 (and_25_out, X[11], Y[12]);
  Full_Adder full_adder_31 (
    .A(and_25_out), .B(full_adder_24_r), .r(full_adder_31_r), .cout(full_adder_31_cout),
    .cin(full_adder_39_cout));
  and and_26 (and_26_out, X[11], Y[8]);
  and and_27 (and_27_out, X[11], Y[9]);
  Full_Adder full_adder_32 (
    .A(and_27_out), .B(and_16_out), .r(full_adder_32_r), .cout(full_adder_32_cout), .cin(full_adder_38_cout));
  and and_28 (and_28_out, X[10], Y[10]);
  Full_Adder full_adder_33 (
    .A(and_28_out), .B(full_adder_32_r), .r(full_adder_33_r), .cout(full_adder_33_cout),
    .cin(full_adder_43_cout));
  and and_29 (and_29_out, X[10], Y[11]);
  Full_Adder full_adder_34 (
    .A(and_29_out), .B(full_adder_29_r), .r(full_adder_34_r), .cout(full_adder_34_cout),
    .cin(full_adder_44_cout));
  and and_30 (and_30_out, X[11], Y[13]);
  Full_Adder full_adder_35 (
    .A(and_30_out), .B(full_adder_25_r), .r(full_adder_35_r), .cout(full_adder_35_cout),
    .cin(full_adder_40_cout));
  and and_31 (and_31_out, X[11], Y[14]);
  Full_Adder full_adder_36 (
    .A(and_31_out), .B(full_adder_26_r), .r(full_adder_36_r), .cout(full_adder_36_cout),
    .cin(full_adder_41_cout));
  nand nand_11 (nand_11_out, X[11], Y[15]);
  Full_Adder full_adder_37 (
    .A(nand_11_out), .B(full_adder_27_r), .r(full_adder_37_r), .cout(full_adder_37_cout),
    .cin(full_adder_42_cout));
  and and_32 (and_32_out, X[10], Y[8]);
  and and_33 (and_33_out, X[10], Y[9]);
  Full_Adder full_adder_38 (
    .A(and_33_out), .B(and_26_out), .r(full_adder_38_r), .cout(full_adder_38_cout), .cin(full_adder_49_cout));
  and and_34 (and_34_out, X[10], Y[12]);
  Full_Adder full_adder_39 (
    .A(and_34_out), .B(full_adder_30_r), .r(full_adder_39_r), .cout(full_adder_39_cout),
    .cin(full_adder_45_cout));
  and and_35 (and_35_out, X[10], Y[13]);
  Full_Adder full_adder_40 (
    .A(and_35_out), .B(full_adder_31_r), .r(full_adder_40_r), .cout(full_adder_40_cout),
    .cin(full_adder_46_cout));
  and and_36 (and_36_out, X[10], Y[14]);
  Full_Adder full_adder_41 (
    .A(and_36_out), .B(full_adder_35_r), .r(full_adder_41_r), .cout(full_adder_41_cout),
    .cin(full_adder_47_cout));
  nand nand_12 (nand_12_out, X[10], Y[15]);
  Full_Adder full_adder_42 (
    .A(nand_12_out), .B(full_adder_36_r), .r(full_adder_42_r), .cout(full_adder_42_cout),
    .cin(full_adder_48_cout));
  and and_37 (and_37_out, X[9], Y[10]);
  Full_Adder full_adder_43 (
    .A(and_37_out), .B(full_adder_38_r), .r(full_adder_43_r), .cout(full_adder_43_cout),
    .cin(half_adder_3_carry));
  and and_38 (and_38_out, X[9], Y[11]);
  Full_Adder full_adder_44 (
    .A(and_38_out), .B(full_adder_33_r), .r(full_adder_44_r), .cout(full_adder_44_cout),
    .cin(half_adder_4_carry));
  and and_39 (and_39_out, X[9], Y[12]);
  Full_Adder full_adder_45 (
    .A(and_39_out), .B(full_adder_34_r), .r(full_adder_45_r), .cout(full_adder_45_cout),
    .cin(half_adder_5_carry));
  and and_40 (and_40_out, X[9], Y[13]);
  Full_Adder full_adder_46 (
    .A(and_40_out), .B(full_adder_39_r), .r(full_adder_46_r), .cout(full_adder_46_cout),
    .cin(half_adder_6_carry));
  and and_41 (and_41_out, X[9], Y[14]);
  Full_Adder full_adder_47 (
    .A(and_41_out), .B(full_adder_40_r), .r(full_adder_47_r), .cout(full_adder_47_cout),
    .cin(half_adder_7_carry));
  nand nand_13 (nand_13_out, X[9], Y[15]);
  Full_Adder full_adder_48 (
    .A(nand_13_out), .B(full_adder_41_r), .r(full_adder_48_r), .cout(full_adder_48_cout),
    .cin(half_adder_8_carry));
  and and_42 (and_42_out, X[9], Y[8]);
  and and_43 (and_43_out, X[9], Y[9]);
  Full_Adder full_adder_49 (
    .A(and_43_out), .B(and_32_out), .r(full_adder_49_r), .cout(full_adder_49_cout), .cin(half_adder_2_carry));
  or or_1 (Overflow, full_adder_48_r, full_adder_42_r, full_adder_37_r, full_adder_28_r, full_adder_21_r, full_adder_13_r, full_adder_7_r, half_adder_1_resultado);
  and and_44 (Resultado[0], X[8], Y[8]);
  and and_45 (and_45_out, X[8], Y[9]);
  Half_Adder half_adder_2 (.A(and_45_out), .B(and_42_out), .Resultado(Resultado[1]), .Carry(half_adder_2_carry));
  and and_46 (and_46_out, X[8], Y[10]);
  Half_Adder half_adder_3 (.A(and_46_out), .B(full_adder_49_r), .Resultado(Resultado[2]), .Carry(half_adder_3_carry));
  and and_47 (and_47_out, X[8], Y[11]);
  Half_Adder half_adder_4 (.A(and_47_out), .B(full_adder_43_r), .Resultado(Resultado[3]), .Carry(half_adder_4_carry));
  and and_48 (and_48_out, X[8], Y[12]);
  Half_Adder half_adder_5 (.A(and_48_out), .B(full_adder_44_r), .Resultado(Resultado[4]), .Carry(half_adder_5_carry));
  and and_49 (and_49_out, X[8], Y[13]);
  Half_Adder half_adder_6 (.A(and_49_out), .B(full_adder_45_r), .Resultado(Resultado[5]), .Carry(half_adder_6_carry));
  and and_50 (and_50_out, X[8], Y[14]);
  Half_Adder half_adder_7 (.A(and_50_out), .B(full_adder_46_r), .Resultado(Resultado[6]), .Carry(half_adder_7_carry));
  nand nand_14 (nand_14_out, X[8], Y[15]);
  Half_Adder half_adder_8 (.A(nand_14_out), .B(full_adder_47_r), .Resultado(Resultado[7]), .Carry(half_adder_8_carry));
endmodule

module DivModule (
  input  Y,
  input  X,
  input  Li,
  input  OS,
  output L0,
  output D
);

  wire and_1_out, and_2_out, and_3_out, and_4_out, not_1_out, not_2_out, xnor_1_out, xor_1_out;

  or or_1 (L0, and_1_out, and_2_out);
  ExactlyOne xor_1 (.out(xor_1_out), .in0(Y), .in1(X), .in2(Li));
  not not_1 (not_1_out, OS);
  and and_1 (and_1_out, Y, not_2_out);
  and and_2 (and_2_out, xnor_1_out, Li);
  and and_3 (and_3_out, xor_1_out, not_1_out);
  or or_2 (D, and_3_out, and_4_out);
  not not_2 (not_2_out, X);
  xnor xnor_1 (xnor_1_out, Y, X);
  and and_4 (and_4_out, X, OS);
endmodule

module Div (
  input  [15:0] Divisor,
  input  [15:0] Dividendo,
  output Div_0,
  output [15:0] Resto,
  output [15:0] Quociente
);

  wire divmodule_1_l0, divmodule_2_d, divmodule_2_l0, divmodule_3_l0, divmodule_4_d, divmodule_4_l0,
       divmodule_5_d, divmodule_5_l0, divmodule_6_l0, divmodule_7_d, divmodule_7_l0, divmodule_8_d,
       divmodule_8_l0, divmodule_9_d, divmodule_9_l0, divmodule_10_d, divmodule_10_l0, divmodule_11_d,
       divmodule_11_l0, divmodule_12_d, divmodule_12_l0, divmodule_13_d, divmodule_13_l0, divmodule_14_l0,
       divmodule_15_l0, divmodule_16_d, divmodule_16_l0, divmodule_17_d, divmodule_17_l0, divmodule_18_d,
       divmodule_18_l0, divmodule_19_d, divmodule_19_l0, divmodule_20_d, divmodule_20_l0, divmodule_21_d,
       divmodule_21_l0, divmodule_22_d, divmodule_22_l0, divmodule_23_d, divmodule_23_l0, divmodule_24_d,
       divmodule_24_l0, divmodule_25_d, divmodule_25_l0, divmodule_26_l0, divmodule_27_d, divmodule_27_l0,
       divmodule_28_l0, divmodule_29_d, divmodule_29_l0, divmodule_30_d, divmodule_30_l0, divmodule_31_d,
       divmodule_31_l0, divmodule_32_d, divmodule_32_l0, divmodule_33_d, divmodule_33_l0, divmodule_34_d,
       divmodule_34_l0, divmodule_35_d, divmodule_35_l0, divmodule_36_l0, divmodule_37_d, divmodule_37_l0,
       divmodule_38_d, divmodule_38_l0, divmodule_39_d, divmodule_39_l0, divmodule_40_d, divmodule_40_l0,
       divmodule_41_d, divmodule_41_l0, divmodule_42_d, divmodule_42_l0, divmodule_43_d, divmodule_43_l0,
       divmodule_44_d, divmodule_44_l0, divmodule_45_d, divmodule_45_l0, divmodule_46_d, divmodule_46_l0,
       divmodule_47_d, divmodule_47_l0, divmodule_48_d, divmodule_48_l0, divmodule_49_d, divmodule_49_l0,
       divmodule_50_l0, divmodule_51_l0, divmodule_52_d, divmodule_52_l0, divmodule_53_d, divmodule_53_l0,
       divmodule_54_d, divmodule_54_l0, divmodule_55_d, divmodule_55_l0, divmodule_56_d, divmodule_56_l0,
       divmodule_57_l0, divmodule_58_d, divmodule_58_l0, divmodule_59_d, divmodule_59_l0, divmodule_60_d,
       divmodule_60_l0, divmodule_61_d, divmodule_61_l0, divmodule_62_d, divmodule_62_l0, divmodule_63_d,
       divmodule_63_l0, divmodule_64_d, divmodule_64_l0, divmodule_65_l0, divmodule_66_l0, divmodule_67_d,
       divmodule_67_l0, divmodule_68_d, divmodule_68_l0, divmodule_69_d, divmodule_69_l0, divmodule_70_l0,
       divmodule_71_l0, divmodule_72_l0;

  nor nor_1 (Div_0, Divisor[0], Divisor[1], Divisor[2], Divisor[3], Divisor[4], Divisor[5], Divisor[6], Divisor[7]);
  not not_1 (Quociente[7], divmodule_1_l0);
  DivModule divmodule_1 (.L0(divmodule_1_l0), .OS(divmodule_1_l0), .Li(divmodule_2_l0), .Y(1'b0), .X(1'b0));  // open: D
  DivModule divmodule_2 (
    .L0(divmodule_2_l0), .OS(divmodule_1_l0), .Li(divmodule_4_l0), .Y(Divisor[15]), .X(1'b0),
    .D(divmodule_2_d));
  DivModule divmodule_3 (
    .L0(divmodule_3_l0), .OS(divmodule_3_l0), .Li(divmodule_5_l0), .Y(1'b0), .X(divmodule_2_d));  // open: D
  not not_2 (Quociente[5], divmodule_6_l0);
  not not_3 (Quociente[6], divmodule_3_l0);
  DivModule divmodule_4 (
    .L0(divmodule_4_l0), .OS(divmodule_1_l0), .Li(divmodule_8_l0), .Y(Divisor[14]), .X(1'b0),
    .D(divmodule_4_d));
  DivModule divmodule_5 (
    .L0(divmodule_5_l0), .OS(divmodule_3_l0), .Li(divmodule_10_l0), .Y(Divisor[15]), .X(divmodule_4_d),
    .D(divmodule_5_d));
  DivModule divmodule_6 (
    .L0(divmodule_6_l0), .OS(divmodule_6_l0), .Li(divmodule_12_l0), .Y(1'b0), .X(divmodule_5_d));  // open: D
  not not_4 (Quociente[4], divmodule_14_l0);
  DivModule divmodule_7 (
    .L0(divmodule_7_l0), .OS(divmodule_1_l0), .Li(divmodule_17_l0), .Y(Divisor[12]), .X(1'b0),
    .D(divmodule_7_d));
  DivModule divmodule_8 (
    .L0(divmodule_8_l0), .OS(divmodule_1_l0), .Li(divmodule_7_l0), .Y(Divisor[13]), .X(1'b0),
    .D(divmodule_8_d));
  DivModule divmodule_9 (
    .L0(divmodule_9_l0), .OS(divmodule_3_l0), .Li(divmodule_19_l0), .Y(Divisor[13]), .X(divmodule_7_d),
    .D(divmodule_9_d));
  DivModule divmodule_10 (
    .L0(divmodule_10_l0), .OS(divmodule_3_l0), .Li(divmodule_9_l0), .Y(Divisor[14]), .X(divmodule_8_d),
    .D(divmodule_10_d));
  DivModule divmodule_11 (
    .L0(divmodule_11_l0), .OS(divmodule_6_l0), .Li(divmodule_20_l0), .Y(Divisor[14]), .X(divmodule_9_d),
    .D(divmodule_11_d));
  DivModule divmodule_12 (
    .L0(divmodule_12_l0), .OS(divmodule_6_l0), .Li(divmodule_11_l0), .Y(Divisor[15]), .X(divmodule_10_d),
    .D(divmodule_12_d));
  DivModule divmodule_13 (
    .L0(divmodule_13_l0), .OS(divmodule_14_l0), .Li(divmodule_22_l0), .Y(Divisor[15]), .X(divmodule_11_d),
    .D(divmodule_13_d));
  DivModule divmodule_14 (
    .L0(divmodule_14_l0), .OS(divmodule_14_l0), .Li(divmodule_13_l0), .Y(1'b0), .X(divmodule_12_d));  // open: D
  DivModule divmodule_15 (
    .L0(divmodule_15_l0), .OS(divmodule_15_l0), .Li(divmodule_24_l0), .Y(1'b0), .X(divmodule_13_d));  // open: D
  not not_5 (Quociente[3], divmodule_15_l0);
  not not_6 (Quociente[2], divmodule_26_l0);
  DivModule divmodule_16 (
    .L0(divmodule_16_l0), .OS(divmodule_1_l0), .Li(divmodule_29_l0), .Y(Divisor[10]), .X(1'b0),
    .D(divmodule_16_d));
  DivModule divmodule_17 (
    .L0(divmodule_17_l0), .OS(divmodule_1_l0), .Li(divmodule_16_l0), .Y(Divisor[11]), .X(1'b0),
    .D(divmodule_17_d));
  DivModule divmodule_18 (
    .L0(divmodule_18_l0), .OS(divmodule_3_l0), .Li(divmodule_30_l0), .Y(Divisor[11]), .X(divmodule_16_d),
    .D(divmodule_18_d));
  DivModule divmodule_19 (
    .L0(divmodule_19_l0), .OS(divmodule_3_l0), .Li(divmodule_18_l0), .Y(Divisor[12]), .X(divmodule_17_d),
    .D(divmodule_19_d));
  DivModule divmodule_20 (
    .L0(divmodule_20_l0), .OS(divmodule_6_l0), .Li(divmodule_21_l0), .Y(Divisor[13]), .X(divmodule_19_d),
    .D(divmodule_20_d));
  DivModule divmodule_21 (
    .L0(divmodule_21_l0), .OS(divmodule_6_l0), .Li(divmodule_31_l0), .Y(Divisor[12]), .X(divmodule_18_d),
    .D(divmodule_21_d));
  DivModule divmodule_22 (
    .L0(divmodule_22_l0), .OS(divmodule_14_l0), .Li(divmodule_23_l0), .Y(Divisor[14]), .X(divmodule_20_d),
    .D(divmodule_22_d));
  DivModule divmodule_23 (
    .L0(divmodule_23_l0), .OS(divmodule_14_l0), .Li(divmodule_32_l0), .Y(Divisor[13]), .X(divmodule_21_d),
    .D(divmodule_23_d));
  DivModule divmodule_24 (
    .L0(divmodule_24_l0), .OS(divmodule_15_l0), .Li(divmodule_25_l0), .Y(Divisor[15]), .X(divmodule_22_d),
    .D(divmodule_24_d));
  DivModule divmodule_25 (
    .L0(divmodule_25_l0), .OS(divmodule_15_l0), .Li(divmodule_33_l0), .Y(Divisor[14]), .X(divmodule_23_d),
    .D(divmodule_25_d));
  DivModule divmodule_26 (
    .L0(divmodule_26_l0), .OS(divmodule_26_l0), .Li(divmodule_27_l0), .Y(1'b0), .X(divmodule_24_d));  // open: D
  DivModule divmodule_27 (
    .L0(divmodule_27_l0), .OS(divmodule_26_l0), .Li(divmodule_34_l0), .Y(Divisor[15]), .X(divmodule_25_d),
    .D(divmodule_27_d));
  DivModule divmodule_28 (
    .L0(divmodule_28_l0), .OS(divmodule_28_l0), .Li(divmodule_35_l0), .Y(1'b0), .X(divmodule_27_d));  // open: D
  not not_7 (Quociente[0], divmodule_36_l0);
  not not_8 (Quociente[1], divmodule_28_l0);
  DivModule divmodule_29 (
    .L0(divmodule_29_l0), .OS(divmodule_1_l0), .Li(divmodule_37_l0), .Y(Divisor[9]), .X(1'b0),
    .D(divmodule_29_d));
  DivModule divmodule_30 (
    .L0(divmodule_30_l0), .OS(divmodule_3_l0), .Li(divmodule_38_l0), .Y(Divisor[10]), .X(divmodule_29_d),
    .D(divmodule_30_d));
  DivModule divmodule_31 (
    .L0(divmodule_31_l0), .OS(divmodule_6_l0), .Li(divmodule_40_l0), .Y(Divisor[11]), .X(divmodule_30_d),
    .D(divmodule_31_d));
  DivModule divmodule_32 (
    .L0(divmodule_32_l0), .OS(divmodule_14_l0), .Li(divmodule_42_l0), .Y(Divisor[12]), .X(divmodule_31_d),
    .D(divmodule_32_d));
  DivModule divmodule_33 (
    .L0(divmodule_33_l0), .OS(divmodule_15_l0), .Li(divmodule_44_l0), .Y(Divisor[13]), .X(divmodule_32_d),
    .D(divmodule_33_d));
  DivModule divmodule_34 (
    .L0(divmodule_34_l0), .OS(divmodule_26_l0), .Li(divmodule_46_l0), .Y(Divisor[14]), .X(divmodule_33_d),
    .D(divmodule_34_d));
  DivModule divmodule_35 (
    .L0(divmodule_35_l0), .OS(divmodule_28_l0), .Li(divmodule_48_l0), .Y(Divisor[15]), .X(divmodule_34_d),
    .D(divmodule_35_d));
  DivModule divmodule_36 (
    .L0(divmodule_36_l0), .OS(divmodule_36_l0), .Li(divmodule_50_l0), .Y(1'b0), .X(divmodule_35_d));  // open: D
  DivModule divmodule_37 (
    .L0(divmodule_37_l0), .OS(divmodule_1_l0), .Li(1'b0), .Y(Divisor[8]), .X(Dividendo[15]),
    .D(divmodule_37_d));
  DivModule divmodule_38 (
    .L0(divmodule_38_l0), .OS(divmodule_3_l0), .Li(divmodule_39_l0), .Y(Divisor[9]), .X(divmodule_37_d),
    .D(divmodule_38_d));
  DivModule divmodule_39 (
    .L0(divmodule_39_l0), .OS(divmodule_3_l0), .Li(1'b0), .Y(Divisor[8]), .X(Dividendo[14]),
    .D(divmodule_39_d));
  DivModule divmodule_40 (
    .L0(divmodule_40_l0), .OS(divmodule_6_l0), .Li(divmodule_41_l0), .Y(Divisor[10]), .X(divmodule_38_d),
    .D(divmodule_40_d));
  DivModule divmodule_41 (
    .L0(divmodule_41_l0), .OS(divmodule_6_l0), .Li(divmodule_52_l0), .Y(Divisor[9]), .X(divmodule_39_d),
    .D(divmodule_41_d));
  DivModule divmodule_42 (
    .L0(divmodule_42_l0), .OS(divmodule_14_l0), .Li(divmodule_43_l0), .Y(Divisor[11]), .X(divmodule_40_d),
    .D(divmodule_42_d));
  DivModule divmodule_43 (
    .L0(divmodule_43_l0), .OS(divmodule_14_l0), .Li(divmodule_53_l0), .Y(Divisor[10]), .X(divmodule_41_d),
    .D(divmodule_43_d));
  DivModule divmodule_44 (
    .L0(divmodule_44_l0), .OS(divmodule_15_l0), .Li(divmodule_45_l0), .Y(Divisor[12]), .X(divmodule_42_d),
    .D(divmodule_44_d));
  DivModule divmodule_45 (
    .L0(divmodule_45_l0), .OS(divmodule_15_l0), .Li(divmodule_54_l0), .Y(Divisor[11]), .X(divmodule_43_d),
    .D(divmodule_45_d));
  DivModule divmodule_46 (
    .L0(divmodule_46_l0), .OS(divmodule_26_l0), .Li(divmodule_47_l0), .Y(Divisor[13]), .X(divmodule_44_d),
    .D(divmodule_46_d));
  DivModule divmodule_47 (
    .L0(divmodule_47_l0), .OS(divmodule_26_l0), .Li(divmodule_55_l0), .Y(Divisor[12]), .X(divmodule_45_d),
    .D(divmodule_47_d));
  DivModule divmodule_48 (
    .L0(divmodule_48_l0), .OS(divmodule_28_l0), .Li(divmodule_49_l0), .Y(Divisor[14]), .X(divmodule_46_d),
    .D(divmodule_48_d));
  DivModule divmodule_49 (
    .L0(divmodule_49_l0), .OS(divmodule_28_l0), .Li(divmodule_56_l0), .Y(Divisor[13]), .X(divmodule_47_d),
    .D(divmodule_49_d));
  DivModule divmodule_50 (
    .L0(divmodule_50_l0), .OS(divmodule_36_l0), .Li(divmodule_51_l0), .Y(Divisor[15]), .X(divmodule_48_d),
    .D(Resto[7]));
  DivModule divmodule_51 (
    .L0(divmodule_51_l0), .OS(divmodule_36_l0), .Li(divmodule_57_l0), .Y(Divisor[14]), .X(divmodule_49_d),
    .D(Resto[6]));
  DivModule divmodule_52 (
    .L0(divmodule_52_l0), .OS(divmodule_6_l0), .Li(1'b0), .Y(Divisor[8]), .X(Dividendo[13]),
    .D(divmodule_52_d));
  DivModule divmodule_53 (
    .L0(divmodule_53_l0), .OS(divmodule_14_l0), .Li(divmodule_58_l0), .Y(Divisor[9]), .X(divmodule_52_d),
    .D(divmodule_53_d));
  DivModule divmodule_54 (
    .L0(divmodule_54_l0), .OS(divmodule_15_l0), .Li(divmodule_59_l0), .Y(Divisor[10]), .X(divmodule_53_d),
    .D(divmodule_54_d));
  DivModule divmodule_55 (
    .L0(divmodule_55_l0), .OS(divmodule_26_l0), .Li(divmodule_62_l0), .Y(Divisor[11]), .X(divmodule_54_d),
    .D(divmodule_55_d));
  DivModule divmodule_56 (
    .L0(divmodule_56_l0), .OS(divmodule_28_l0), .Li(divmodule_63_l0), .Y(Divisor[12]), .X(divmodule_55_d),
    .D(divmodule_56_d));
  DivModule divmodule_57 (
    .L0(divmodule_57_l0), .OS(divmodule_36_l0), .Li(divmodule_66_l0), .Y(Divisor[13]), .X(divmodule_56_d),
    .D(Resto[5]));
  DivModule divmodule_58 (
    .L0(divmodule_58_l0), .OS(divmodule_14_l0), .Li(1'b0), .Y(Divisor[8]), .X(Dividendo[12]),
    .D(divmodule_58_d));
  DivModule divmodule_59 (
    .L0(divmodule_59_l0), .OS(divmodule_15_l0), .Li(divmodule_60_l0), .Y(Divisor[9]), .X(divmodule_58_d),
    .D(divmodule_59_d));
  DivModule divmodule_60 (
    .L0(divmodule_60_l0), .OS(divmodule_15_l0), .Li(1'b0), .Y(Divisor[8]), .X(Dividendo[11]),
    .D(divmodule_60_d));
  DivModule divmodule_61 (
    .L0(divmodule_61_l0), .OS(divmodule_26_l0), .Li(divmodule_67_l0), .Y(Divisor[9]), .X(divmodule_60_d),
    .D(divmodule_61_d));
  DivModule divmodule_62 (
    .L0(divmodule_62_l0), .OS(divmodule_26_l0), .Li(divmodule_61_l0), .Y(Divisor[10]), .X(divmodule_59_d),
    .D(divmodule_62_d));
  DivModule divmodule_63 (
    .L0(divmodule_63_l0), .OS(divmodule_28_l0), .Li(divmodule_64_l0), .Y(Divisor[11]), .X(divmodule_62_d),
    .D(divmodule_63_d));
  DivModule divmodule_64 (
    .L0(divmodule_64_l0), .OS(divmodule_28_l0), .Li(divmodule_68_l0), .Y(Divisor[10]), .X(divmodule_61_d),
    .D(divmodule_64_d));
  DivModule divmodule_65 (
    .L0(divmodule_65_l0), .OS(divmodule_36_l0), .Li(divmodule_71_l0), .Y(Divisor[11]), .X(divmodule_64_d),
    .D(Resto[3]));
  DivModule divmodule_66 (
    .L0(divmodule_66_l0), .OS(divmodule_36_l0), .Li(divmodule_65_l0), .Y(Divisor[12]), .X(divmodule_63_d),
    .D(Resto[4]));
  DivModule divmodule_67 (
    .L0(divmodule_67_l0), .OS(divmodule_26_l0), .Li(1'b0), .Y(Divisor[8]), .X(Dividendo[10]),
    .D(divmodule_67_d));
  DivModule divmodule_68 (
    .L0(divmodule_68_l0), .OS(divmodule_28_l0), .Li(divmodule_69_l0), .Y(Divisor[9]), .X(divmodule_67_d),
    .D(divmodule_68_d));
  DivModule divmodule_69 (
    .L0(divmodule_69_l0), .OS(divmodule_28_l0), .Li(1'b0), .Y(Divisor[8]), .X(Dividendo[9]),
    .D(divmodule_69_d));
  DivModule divmodule_70 (
    .L0(divmodule_70_l0), .OS(divmodule_36_l0), .Li(divmodule_72_l0), .Y(Divisor[9]), .X(divmodule_69_d),
    .D(Resto[1]));
  DivModule divmodule_71 (
    .L0(divmodule_71_l0), .OS(divmodule_36_l0), .Li(divmodule_70_l0), .Y(Divisor[10]), .X(divmodule_68_d),
    .D(Resto[2]));
  DivModule divmodule_72 (
    .L0(divmodule_72_l0), .OS(divmodule_36_l0), .Li(1'b0), .Y(Divisor[8]), .X(Dividendo[8]), .D(Resto[0]));
endmodule
